# Fritzing sketch duke-distancesensor (saved by Fritzing 0.9.3b)
breadboards: 1

parts:
  Raspberry_Pi_1 = Raspberry Pi 3 [part_number=RPI-3-V1.2]
  hc-sr1 = hc-sr04
  R1 = Resistor [tolerance=±5% resistance=330 package=THT]
  R2 = Resistor [tolerance=±5% resistance=330 package=THT]
  R3 = Resistor [tolerance=±5% resistance=100 package=THT]

nets:
  GND: Raspberry_Pi_1.GND, hc-sr1.GND, R3.Pin_0
  N1: Raspberry_Pi_1.GIPO24, R1.Pin_1, R2.Pin_1
  N2: Raspberry_Pi_1.GIPO18, hc-sr1.Trig
  5V: Raspberry_Pi_1.5V, hc-sr1.VCC
  N3: hc-sr1.Echo, R1.Pin_0
  N4: R2.Pin_0, R3.Pin_1
